# Fritzing sketch schematic (saved by Fritzing 0.9.3b)

parts:
  WeMos_D1_Mini1 = WeMos D1 Mini
  U1 = mystery part, 8 pins [chip_label="Nokia 5110"]
  S2 = Pushbutton [package=THT]

nets:
  3.3V: WeMos_D1_Mini1.3V3, U1.pin6
  PWR in via USB: WeMos_D1_Mini1.5V
  N1: WeMos_D1_Mini1.D1, U1.pin1
  N2: WeMos_D1_Mini1.D2, U1.pin2
  N3: WeMos_D1_Mini1.D3, U1.pin3
  N4: WeMos_D1_Mini1.D4, U1.pin7
  N5: WeMos_D1_Mini1.D5, U1.pin5
  N6: WeMos_D1_Mini1.D6, S2.leg1
  N7: WeMos_D1_Mini1.D7, U1.pin4
  GND: WeMos_D1_Mini1.G, U1.pin8, S2.leg0
